// Logisim project project1.circ as structural Verilog: 1 circuit, main circuit main
module main (
  input  [3:0] I1,
  input  [3:0] I2
);

  wire _2, _3, _4, adder_1_cout, and_1_out, and_2_out, and_3_out, and_4_out, and_5_out, nor_1_out, or_1_out,
       or_2_out, or_4_out, xor_1_out, xor_2_out;
  wire [3:0] adder_1_out, bit_extender_1_out, controlled_buffer_1_out, controlled_buffer_2_out,
       controlled_buffer_3_out, divider_1_out, divider_1_rem, multiplexer_3_out, multiplexer_4_out;

  Hex_Digit_Display hex_digit_display_1 (.value(I1));  // open: dp
  or or_1 (or_1_out, adder_1_out[1], adder_1_out[2], adder_1_out[3]);
  and and_1 (and_1_out, adder_1_out[3], adder_1_out[0]);
  and and_2 (and_2_out, adder_1_out[0], adder_1_out[1]);
  and and_3 (and_3_out, adder_1_out[1], adder_1_out[2]);
  and and_4 (and_4_out, adder_1_out[2], adder_1_out[3]);
  nor nor_1 (nor_1_out, adder_1_out[0], adder_1_out[1]);
  or or_2 (or_2_out, adder_1_out[2], adder_1_out[3]);
  Hex_Digit_Display hex_digit_display_2 (.value(I2));  // open: dp
  xor xor_1 (xor_1_out, adder_1_out[0], or_1_out);
  Hex_Digit_Display hex_digit_display_3 (.value(adder_1_out));  // open: dp
  Hex_Digit_Display hex_digit_display_4 (.value(bit_extender_1_out));  // open: dp
  Adder #(.width(4)) adder_1 (.a(I1), .b(I2), .out(adder_1_out), .cout(adder_1_cout));  // open: cin
  Multiplexer #(.enable("false")) multiplexer_1 (.in0(xor_1_out), .in1(1'b0), .out(_2), .sel(adder_1_out[0]));
  and and_5 (and_5_out, and_1_out, and_4_out, and_3_out, and_3_out);
  or or_3 (_3, and_5_out, xor_2_out);
  ExactlyOne xor_2 (.out(xor_2_out), .in0(and_1_out), .in1(and_2_out), .in2(and_3_out), .in3(and_4_out));
  Multiplexer #(.enable("false")) multiplexer_2 (.in0(nor_1_out), .in1(or_2_out), .out(_4), .sel(nor_1_out));
  Hex_Digit_Display hex_digit_display_5 (.value(multiplexer_4_out));  // open: dp
  assign bit_extender_1_out = {{3{1'b0}}, adder_1_cout};  // Bit_Extender bit_extender_1
  LED led_1 (.in(_2));
  LED led_2 (.in(_3));
  LED led_3 (.in(_4));
  Hex_Digit_Display hex_digit_display_6 (.value(divider_1_out));  // open: dp
  Divider #(.width(4)) divider_1 (
    .a(adder_1_out), .b(multiplexer_4_out), .out(divider_1_out), .upper(bit_extender_1_out),
    .rem(divider_1_rem));
  Hex_Digit_Display hex_digit_display_7 (.value(divider_1_rem));  // open: dp
  assign controlled_buffer_1_out = _3 ? 4'b0011 : 4'bz;  // Controlled_Buffer controlled_buffer_1
  assign controlled_buffer_2_out = _2 ? 4'b0010 : 4'bz;  // Controlled_Buffer controlled_buffer_2
  Multiplexer #(.width(4), .enable("false")) multiplexer_3 (
    .in0(controlled_buffer_1_out), .in1(controlled_buffer_3_out), .out(multiplexer_3_out), .sel(_4));
  assign controlled_buffer_3_out = _4 ? 4'b0100 : 4'bz;  // Controlled_Buffer controlled_buffer_3
  Multiplexer #(.width(4), .enable("false")) multiplexer_4 (
    .in0(controlled_buffer_2_out), .in1(multiplexer_3_out), .out(multiplexer_4_out), .sel(or_4_out));
  or or_4 (or_4_out, _3, _4);

  // Notes on the sheet:
  //   Author: Christian Carreras
  //   Date Created: 09/08/2014
  //   CSC 235 Dr. Spiegel
  //   Purpose: Takes two input values
  //   finds their sum and checks
  //   if that sum is divisable by 2, 3 and 4
  //   Input Values
  //   * Only works for sums ≤ 15 (F) *
  //   Uses logical nor to check for the 0 and 1 bits
  //   I1
  //   +
  //   I2
  //   =
  //   Adder:
  //   - finds the sum of the
  //   two input values
  //   If bits 0, 1 or both are present, automatically not divisable by 4. Multiplexer denies power to LED.
  //   If bits 2, 3 or both are present without the presence of bits 0, 1 or both automically makes sum divisable by 4
  //   Due Date: 09/17/2014
  //   Sum
  //   16^1
  //   16^0
  //   Carry to be displayed
  //   cout from adder sends carry
  //   to bit extender to Hex display
  //   ÷
  //   Last checks the set {0, 1, 2, 3} for a match
  //   Q
  //   =
  //   Divider
  //   Divisable by 2
  //   Essestially, if the 0 bit is used, will not be divisable by two
  //   Uses logical or on other bits, and xor with zero bit
  //   Then uses multiplexer to make sure 0 did not pass through xor
  //   Divisable by 3
  //   Uses logical and with the bits as follows (in set notation):
  //   Then uses logica xor to make sure only one set passes through
  //   Divisable by 4
  //   R
  //   * Divider used only for testing/debugging purposes *
  //   {0, 1}, {1, 2}, {0, 3}, {2, 3}
  //   Finds highest divisor value
  //   and sends to the divider
  //   If no divisor is present, then
  //   no divisor is sent.
endmodule
