// Logisim project csc235_project3.circ as structural Verilog: 1 circuit, main circuit main
module main (
  input  [3:0] in_1,
  input  [1:0] in_2
);

  wire and_1_out, and_2_out, clock_1_out, d_ff_1_q, nand_1_out, nand_2_out, nand_3_out, nand_4_out,
       nand_5_out, nand_6_out, nand_7_out, nand_8_out, not_1_out, not_2_out, not_3_out, not_4_out, not_5_out,
       not_6_out, not_7_out, not_8_out, not_9_out, not_10_out, not_11_out, not_12_out, not_13_out,
       not_14_out, not_15_out, not_16_out, not_17_out, or_1_out, or_2_out, or_3_out, or_4_out, or_5_out,
       or_6_out, T1, T3;
  wire [3:0] adder_1_out, counter_1_q, multiplexer_1_out, multiplexer_2_out, T2, T4;

  not not_1 (not_1_out, in_1[3]);
  not not_2 (not_2_out, in_1[2]);
  and and_1 (and_1_out, not_2_out, not_3_out);
  not not_3 (not_3_out, in_1[1]);
  D_Flip_Flop d_ff_1 (.clk(clock_1_out), .D(nand_1_out), .Q(d_ff_1_q));  // open: Qn, preset, en, reset
  nand nand_1 (nand_1_out, 1'b0, T1);
  not not_4 (not_4_out, in_2[1]);
  assign T4 = {{2{1'b0}}, in_2};  // Bit_Extender bit_extender_1
  Multiplexer #(.width(4)) multiplexer_1 (
    .in0(4'b0000), .in1(in_1), .out(multiplexer_1_out), .sel(or_1_out));  // open: en
  or or_1 (or_1_out, not_1_out, and_1_out);
  D_Flip_Flop d_ff_2 (.clk(clock_1_out), .D(d_ff_1_q), .Q(T1));  // open: Qn, preset, en, reset
  and and_2 (and_2_out, in_2[0], not_4_out);
  Multiplexer #(.width(4)) multiplexer_2 (
    .in0(multiplexer_1_out), .in1(T2), .out(multiplexer_2_out), .sel(T1));  // open: en
  Clock clock_1 (.out(clock_1_out));
  and and_3 (T3, and_2_out, T1);
  not not_5 (not_5_out, T3);
  Counter #(.width(4), .max('h9)) counter_1 (
    .load(not_5_out), .D(multiplexer_2_out), .count(T3), .Q(counter_1_q), .clk(clock_1_out));  // open: carry, clr
  or or_2 (or_2_out, counter_1_q[0], counter_1_q[1], counter_1_q[2], counter_1_q[3]);
  not not_6 (not_6_out, counter_1_q[2]);
  not not_7 (not_7_out, counter_1_q[1]);
  not not_8 (not_8_out, counter_1_q[0]);
  nand nand_2 (nand_2_out, counter_1_q[3], counter_1_q[0]);
  nand nand_3 (nand_3_out, counter_1_q[2], counter_1_q[1], not_9_out);
  not not_9 (not_9_out, counter_1_q[0]);
  not not_10 (not_10_out, counter_1_q[2]);
  nand nand_4 (nand_4_out, not_10_out, counter_1_q[1], counter_1_q[0]);
  or or_3 (or_3_out, counter_1_q[3], counter_1_q[2]);
  nand nand_5 (nand_5_out, counter_1_q[2], counter_1_q[1], counter_1_q[0]);
  Hex_Digit_Display hex_digit_display_1 (.value(counter_1_q));  // open: dp
  nand nand_6 (nand_6_out, counter_1_q[1], not_6_out);
  not not_11 (not_11_out, nand_6_out);
  not not_12 (not_12_out, nand_7_out);
  nand nand_7 (nand_7_out, counter_1_q[2], not_7_out, counter_1_q[0]);
  not not_13 (not_13_out, nand_8_out);
  nand nand_8 (nand_8_out, counter_1_q[1], not_8_out);
  not not_14 (not_14_out, nand_2_out);
  not not_15 (not_15_out, nand_3_out);
  not not_16 (not_16_out, nand_4_out);
  or or_4 (or_4_out, counter_1_q[3], not_17_out);
  not not_17 (not_17_out, nand_5_out);
  or or_5 (or_5_out, counter_1_q[3], not_11_out, not_12_out, not_13_out);
  _7_Segment_Display u_7_segment_display_1 (
    .g(or_5_out), .f(or_3_out), .a(or_2_out), .e(or_4_out), .d(or_6_out));  // open: b, c, dp
  or or_6 (or_6_out, not_14_out, not_15_out, not_16_out);
  Adder #(.width(4)) adder_1 (.a(counter_1_q), .b(T4), .out(adder_1_out));  // open: cin, cout
  Divider #(.width(4)) divider_1 (.a(adder_1_out), .b(4'b1010), .rem(T2));  // open: out, upper

  // Notes on the sheet:
  //   Select a 2-bit number
  //   the adder and divider
  //   Author: Christian Carreras
  //   File: csc235_project3
  //   Date Created: 10/20/2014
  //   Due Date: 10/29/2014
  //   Choose value to be added to counter
  //   value is a 4-bit number
  //   Only values 0-9 may be added
  //   If input is greater than 9
  //   0 will be entered instead
  //   has successfully been loaded into the counter.
  //   load has a chance to appear.
  //   The number selected is the increment value
  //   If 0: number in the counter will stay the same
  //   If 3: same as 2 but with 3 as the increment value
  //   Next value to be loaded
  //   Memory devices deactivates the load after a number
  //   At this point no value can be loaded after simulation
  //   has started. Also delays load by one tick so the original
  //   If 1: will use the count pin on the counter to increment by 1
  //   If 2: will take the current value and increment by 2 via adder & divider
  //   Also extends the 2-bit value to a 4-bit value to send to
  //   a value has been loaded.
  //   Tunnel(T4) takes increment value to the adder
  //   Class: CSC 235
  //   Term: Fall 2014
  //   _
  //   Tunnel(T1) will take delayed value to a
  //   multiplexor to select the next value after
  //   Tunnel(T3) takes value to see
  //   if count pin should be used or
  //   if the load should be used
  //   If increment value is 1: count is 1 and load is 0. Otherwise load is 1 and count is 0
  //   Top:
  //   A + B + C +D
  //   Center:
  //   _
  //   A + CD + BC+ BCD
  //   Bottom:
  //   _
  //   _
  //   AD + BCD + BCD
  //   Upper Left:
  //   A + B
  //   Lower Left:
  //   A + BCD
  //   Purpose: Displays the values 0-9 on a 7 segment device that lights up certain segments depending on the number.
  //   A counter is used with a clock to enter the digits 0-9 into the circuits which find which segments should be lit.
  //   The counter can increment or decrement by the default value of 1 or increment by the value added by the adder.
  //   *Numbers restricted to 0-9*
  //   Displays number in decimal notation
  //   Adds current value in the counter
  //   with the selected increment
  //   value (only 2 and 3 do this)
  //   Display in new number notation
  //   segment combinations correlate to certain numbers
  //   remainder, this gets rid of
  //   overflow problems
  //   Tunnel (T2) takes incremented value to
  //   the multiplexor to be loaded into the counter
  //   Divide by 10 and send away the
endmodule
