// Logisim project Counter.circ as structural Verilog: 1 circuit, main circuit main
// Clock
module main (
  output out_1
);

  wire [1:0] counter_1_q;

  Clock clock_1 (.out(out_1));
  Counter #(.width(2), .max('h3)) counter_1 (.Q(counter_1_q), .clk(out_1));  // open: load, D, count, carry, clr
  Register #(.width(2)) register_1 (.D(counter_1_q), .clk(out_1));  // open: en, Q, clr
endmodule
